// Logisim project CPU.circ as structural Verilog: 4 circuits, main circuit main
module main (
  output [7:0] address,
  output [7:0] r0,
  output [1:0] addrsel,
  output [7:0] r1,
  output [7:0] r2,
  output [7:0] r3,
  output [7:0] datain,
  output [1:0] aluop,
  output [7:0] dval,
  output [7:0] dbus,
  output [7:0] aluout,
  output [7:0] sbus,
  output [1:0] out_13,
  output pcsel,
  output [1:0] phase,
  output pcload
);

  wire clock_1_out, clock_2_out, clock_3_out, clock_4_out, dwrite, imload, irload, readwrite,
       register_file_1_negative, register_file_1_zero;
  wire [1:0] dregsel, sregsel;
  wire [7:0] multiplexer_3_out, pc_adder_1_pc_out, register_1_q, register_2_q, register_3_q;

  Clock clock_1 (.out(clock_1_out));
  RAM #(.bus("separate")) ram_1 (
    .addr(address), .din(dbus), .data(datain), .str(readwrite), .clk(clock_1_out));  // open: sel, ld, clr
  Multiplexer #(.select(2), .width(8), .enable("false")) multiplexer_1 (
    .in0(register_3_q), .in1(register_2_q), .in2(sbus), .in3(dbus), .out(address), .sel(addrsel));
  Register register_1 (.D(datain), .en(irload), .Q(register_1_q), .clk(clock_2_out));  // open: clr
  Clock clock_2 (.out(clock_2_out));
  Decode_Logic decode_logic_1 (
    .addrsel(addrsel), .irvalue(register_1_q), .irload(irload), .imload(imload), .dwrite(dwrite),
    .dregsel(dregsel), .sregsel(sregsel), .aluop(aluop), .regsel(out_13), .phase(phase),
    .readwrite(readwrite), .pcsel(pcsel), .zero(register_file_1_zero), .negative(register_file_1_negative),
    .pcload(pcload));
  Register register_2 (.D(datain), .en(imload), .Q(register_2_q), .clk(clock_3_out));  // open: clr
  Clock clock_3 (.out(clock_3_out));
  Multiplexer #(.select(2), .width(8), .enable("false")) multiplexer_2 (
    .in0(register_2_q), .in1(sbus), .in2(datain), .in3(aluout), .out(dval), .sel(out_13));
  Multiplexer #(.width(8), .enable("false")) multiplexer_3 (
    .in0(register_2_q), .in1(pc_adder_1_pc_out), .out(multiplexer_3_out), .sel(pcsel));
  PC_Adder pc_adder_1 (.PC_in(register_3_q), .PC_out(pc_adder_1_pc_out));
  Register register_3 (.D(multiplexer_3_out), .en(pcload), .Q(register_3_q), .clk(clock_4_out));  // open: clr
  Clock clock_4 (.out(clock_4_out));
  Register_File register_file_1 (
    .dbus(dbus), .sbus(sbus), .dregsel(dregsel), .sregsel(sregsel), .dval(dval), .dwrite(dwrite), .r0(r0),
    .r1(r1), .r2(r2), .r3(r3), .Zero(register_file_1_zero), .Negative(register_file_1_negative));
  // ALU alu_1: pin names not known; wires that end beside it: dbus, sbus, aluop, aluout

  // Other names for the same wires on the sheet: regsel[1:0] = out_13

  // Notes on the sheet:
  //   address bus
  //   RAM
  //   dataout bus
  //   datain   bus
  //   IR
  //   Decode
  //   Logic
  //   Immed
  //   8-bit Hardwired CPU
  //   PC
  //   +
  //   PC Adder
  //   Regs
  //   Register
  //   Values
  //   ALU
endmodule

module Register_File (
  input  dwrite,
  input  [1:0] dregsel,
  input  [7:0] dval,
  input  [1:0] sregsel,
  output [7:0] r0,
  output [7:0] dbus,
  output [7:0] r1,
  output Zero,
  output [7:0] r2,
  output [7:0] r3,
  output Negative,
  output [7:0] sbus
);

  wire clock_1_out, demultiplexer_1_out0, demultiplexer_1_out1, demultiplexer_1_out2, demultiplexer_1_out3,
       or_1_out;

  Demultiplexer #(.select(2), .enable("false")) demultiplexer_1 (
    .out0(demultiplexer_1_out0), .out1(demultiplexer_1_out1), .out2(demultiplexer_1_out2),
    .out3(demultiplexer_1_out3), .in(dwrite), .sel(dregsel));
  Clock clock_1 (.out(clock_1_out));
  Register register_1 (.D(dval), .en(demultiplexer_1_out0), .Q(r0), .clk(clock_1_out));  // open: clr
  Register register_2 (.D(dval), .en(demultiplexer_1_out1), .Q(r1), .clk(clock_1_out));  // open: clr
  Register register_3 (.D(dval), .en(demultiplexer_1_out2), .Q(r2), .clk(clock_1_out));  // open: clr
  Register register_4 (.D(dval), .en(demultiplexer_1_out3), .Q(r3), .clk(clock_1_out));  // open: clr
  Multiplexer #(.select(2), .width(8), .enable("false")) multiplexer_1 (
    .in0(r0), .in1(r1), .in2(r2), .in3(r3), .out(dbus), .sel(dregsel));
  Multiplexer #(.select(2), .width(8), .enable("false")) multiplexer_2 (
    .in0(r0), .in1(r1), .in2(r2), .in3(r3), .out(sbus), .sel(sregsel));
  or or_1 (or_1_out, dbus[0], dbus[1], dbus[2], dbus[3], dbus[4], dbus[5], dbus[6], dbus[7]);
  not not_1 (Zero, or_1_out);

  assign Negative = dbus[7];

  // Other names for the same wires on the sheet: drs[1:0] = dregsel

  // Notes on the sheet:
  //   Register File
endmodule

module PC_Adder (
  input  [7:0] PC_in,
  output [7:0] PC_out
);

  Adder adder_1 (.a(PC_in), .b(8'h1), .out(PC_out), .cin(1'b0));  // open: cout

  // Notes on the sheet:
  //   PC Adder
endmodule

module Decode_Logic (
  input  [7:0] irvalue,
  input  zero,
  input  negative,
  output [1:0] phase,
  output [1:0] dregsel,
  output [1:0] sregsel,
  output [1:0] aluop,
  output irload,
  output imload,
  output pcsel,
  output readwrite,
  output pcload,
  output [1:0] regsel,
  output dwrite,
  output [1:0] addrsel
);

  wire and_1_out, and_2_out, and_3_out, and_4_out, and_5_out, clock_1_out, multiplexer_3_out,
       multiplexer_7_out, not_1_out, not_2_out, not_3_out, not_4_out, or_1_out;
  wire [1:0] multiplexer_1_out, multiplexer_11_out;

  not not_1 (not_1_out, zero);
  not not_2 (not_2_out, negative);
  and and_1 (and_1_out, not_1_out, not_2_out);
  Multiplexer #(.select(4), .width(2), .enable("false")) multiplexer_1 (
    .in0(2'b11), .in1(2'b11), .in2(2'b11), .in3(2'b11), .in4(2'b10), .in5(2'b00), .in6(2'b01), .in7(2'b00),
    .in8(2'b00), .in9(2'b00), .in10(2'b00), .in11(2'b00), .in12(2'b10), .in13(2'b00), .in14(2'b00),
    .in15(2'b00), .out(multiplexer_1_out), .sel(irvalue[7:4]));
  Multiplexer #(.select(2), .enable("false")) multiplexer_2 (
    .in0(1'b1), .in1(1'b0), .in2(1'b0), .in3(1'b0), .out(irload), .sel(phase));
  not not_3 (not_3_out, irvalue[6]);
  Multiplexer #(.select(2), .enable("false")) multiplexer_3 (
    .in0(zero), .in1(not_1_out), .in2(and_1_out), .in3(negative), .out(multiplexer_3_out), .sel(irvalue[5:4]));
  and and_2 (and_2_out, not_3_out, irvalue[7], multiplexer_3_out);
  and and_3 (and_3_out, irvalue[4], irvalue[5], irvalue[6], irvalue[7]);
  Multiplexer #(.select(2), .width(2), .enable("false")) multiplexer_4 (
    .in0(2'b00), .in1(2'b00), .in2(multiplexer_1_out), .in3(2'b00), .out(regsel), .sel(phase));
  or or_1 (or_1_out, and_2_out, and_3_out);
  Multiplexer #(.select(2), .enable("false")) multiplexer_5 (
    .in0(1'b1), .in1(irvalue[7]), .in2(or_1_out), .in3(1'b0), .out(pcload), .sel(phase));
  Multiplexer #(.select(2), .enable("false")) multiplexer_6 (
    .in0(1'b0), .in1(irvalue[7]), .in2(1'b0), .in3(1'b0), .out(imload), .sel(phase));
  Multiplexer #(.select(4), .enable("false")) multiplexer_7 (
    .in0(1'b1), .in1(1'b1), .in2(1'b1), .in3(1'b1), .in4(1'b1), .in5(1'b0), .in6(1'b1), .in7(1'b0),
    .in8(1'b0), .in9(1'b0), .in10(1'b0), .in11(1'b0), .in12(1'b1), .in13(1'b0), .in14(1'b1), .in15(1'b0),
    .out(multiplexer_7_out), .sel(irvalue[7:4]));
  Counter #(.width(2), .max('h3)) counter_1 (
    .Q(phase), .clk(clock_1_out), .clr(and_4_out));  // open: load, D, count, carry
  and and_4 (and_4_out, phase[1], phase[0]);
  Clock clock_1 (.out(clock_1_out));
  not not_4 (not_4_out, irvalue[5]);
  Multiplexer #(.select(2), .enable("false")) multiplexer_8 (
    .in0(1'b0), .in1(1'b0), .in2(multiplexer_7_out), .in3(1'b0), .out(dwrite), .sel(phase));
  Multiplexer #(.select(2), .enable("false")) multiplexer_9 (
    .in0(1'b1), .in1(1'b1), .in2(1'b0), .in3(1'b0), .out(pcsel), .sel(phase));
  and and_5 (and_5_out, irvalue[4], not_4_out, irvalue[6]);
  Multiplexer #(.select(2), .enable("false")) multiplexer_10 (
    .in0(1'b0), .in1(1'b0), .in2(and_5_out), .in3(1'b0), .out(readwrite), .sel(phase));
  Multiplexer #(.select(4), .width(2), .enable("false")) multiplexer_11 (
    .in0(2'b00), .in1(2'b00), .in2(2'b00), .in3(2'b00), .in4(2'b10), .in5(2'b10), .in6(2'b00), .in7(2'b00),
    .in8(2'b00), .in9(2'b00), .in10(2'b00), .in11(2'b00), .in12(2'b01), .in13(2'b01), .in14(2'b00),
    .in15(2'b00), .out(multiplexer_11_out), .sel(irvalue[7:4]));
  Multiplexer #(.select(2), .width(2), .enable("false")) multiplexer_12 (
    .in0(2'b00), .in1(2'b00), .in2(multiplexer_11_out), .in3(2'b00), .out(addrsel), .sel(phase));

  assign aluop = irvalue[5:4];
  assign dregsel = irvalue[3:2];
  assign sregsel = irvalue[1:0];

  // Other names for the same wires on the sheet: irbit4 = irvalue[4]; op1op2[3:0] = irvalue[7:4];
  //   op2[1:0] = irvalue[5:4]; irbit5 = irvalue[5]; irbit6 = irvalue[6]; op1[1:0] = irvalue[7:6]; irbit7 = irvalue[7];
  //   rd[1:0] = irvalue[3:2]; rs[1:0] = irvalue[1:0]

  // Notes on the sheet:
  //   IR Load
  //   PC Load
  //   Register Select
  //   Immed Load
  //   Decode Logic
  //   Dest Reg Write
  //   Phase
  //   Counter
  //   PC Select
  //   Read/Write
  //   Address Select
endmodule
