// Logisim project EXERCICIO ULA.circ as structural Verilog: 8 circuits, main circuit PROTOTIPO ULA
module PROTOTIPO_ULA (
  input  [3:0] in_1,
  input  [3:0] in_2,
  input  [1:0] in_3,
  output [3:0] out_4
);

  wire adder_1_cout, subtractor_1_bout, undriven, undriven_2;
  wire [3:0] adder_1_out, and_1_out, multiplier_1_cout, multiplier_1_out, subtractor_1_out, undriven_3;

  Adder #(.width(4)) adder_1 (.a(in_2), .b(in_1), .out(adder_1_out), .cin(undriven), .cout(adder_1_cout));
  Subtractor #(.width(4)) subtractor_1 (
    .a(in_2), .b(in_1), .out(subtractor_1_out), .bin(undriven_2), .bout(subtractor_1_bout));
  Multiplier #(.width(4)) multiplier_1 (
    .a(in_2), .b(in_1), .out(multiplier_1_out), .cin(undriven_3), .cout(multiplier_1_cout));
  assign and_1_out = in_2 & in_1;  // AND_Gate and_1, 4 bits wide
  Multiplexer #(.select(2), .width(4)) multiplexer_1 (
    .in0(adder_1_out), .in1(subtractor_1_out), .in2(multiplier_1_out), .in3(and_1_out), .out(out_4),
    .sel(in_3));  // open: en
endmodule

module ULA (
  input  in_1,
  input  in_2,
  input  in_3,
  input  in_4,
  input  in_5,
  input  in_6,
  input  in_7,
  input  in_8,
  input  in_9,
  input  in_10,
  input  in_11,
  input  in_12,
  input  in_13,
  input  in_14,
  input  in_15,
  input  in_16,
  input  in_17,
  output out_18,
  output out_19,
  output out_20,
  output out_21
);

  wire and_1_out, multiplexador_1_out_7, multiplexador_2_out_7, multiplexador_3_out_7, multiplexador_4_out_7,
       multiplicador_1_out_6, multiplicador_1_out_7, multiplicador_1_out_8, multiplicador_1_out_9,
       registrador_1_q, registrador_2_q, registrador_3_q, registrador_4_q, registrador_5_q, registrador_6_q,
       registrador_7_q, registrador_8_q, somador_completo_1_c_out, somador_completo_1_s,
       somador_completo_2_c_out, somador_completo_2_s, somador_completo_3_c_out, somador_completo_3_s,
       somador_completo_4_c_out, somador_completo_4_s, subtrator_completo_1_c_out, subtrator_completo_1_s,
       subtrator_completo_2_c_out, subtrator_completo_2_s, subtrator_completo_3_c_out,
       subtrator_completo_3_s, subtrator_completo_4_c_out, subtrator_completo_4_s;

  registrador registrador_1 (.D(in_1), .enable(in_17), .Clock(in_16), .Q(registrador_1_q));  // open: Q_prime
  registrador registrador_2 (.D(in_2), .enable(in_17), .Clock(in_16), .Q(registrador_2_q));  // open: Q_prime
  registrador registrador_3 (.D(in_3), .enable(in_17), .Clock(in_16), .Q(registrador_3_q));  // open: Q_prime
  registrador registrador_4 (.D(in_4), .enable(in_17), .Clock(in_16), .Q(registrador_4_q));  // open: Q_prime
  somador_completo somador_completo_1 (
    .A(registrador_4_q), .B(registrador_5_q), .C(in_9), .S(somador_completo_1_s),
    .C_OUT(somador_completo_1_c_out));
  somador_completo somador_completo_2 (
    .A(registrador_3_q), .B(registrador_6_q), .C(somador_completo_1_c_out), .S(somador_completo_2_s),
    .C_OUT(somador_completo_2_c_out));
  somador_completo somador_completo_3 (
    .A(registrador_2_q), .B(registrador_7_q), .C(somador_completo_2_c_out), .S(somador_completo_3_s),
    .C_OUT(somador_completo_3_c_out));
  somador_completo somador_completo_4 (
    .A(registrador_1_q), .B(registrador_8_q), .C(somador_completo_3_c_out), .S(somador_completo_4_s),
    .C_OUT(somador_completo_4_c_out));
  subtrator_completo subtrator_completo_1 (
    .A(registrador_4_q), .B(registrador_5_q), .C(in_11), .S(subtrator_completo_1_s),
    .C_OUT(subtrator_completo_1_c_out));
  subtrator_completo subtrator_completo_2 (
    .A(registrador_3_q), .B(registrador_6_q), .C(subtrator_completo_1_c_out), .S(subtrator_completo_2_s),
    .C_OUT(subtrator_completo_2_c_out));
  subtrator_completo subtrator_completo_3 (
    .A(registrador_2_q), .B(registrador_7_q), .C(subtrator_completo_2_c_out), .S(subtrator_completo_3_s),
    .C_OUT(subtrator_completo_3_c_out));
  subtrator_completo subtrator_completo_4 (
    .A(registrador_1_q), .B(registrador_8_q), .C(subtrator_completo_3_c_out), .S(subtrator_completo_4_s),
    .C_OUT(subtrator_completo_4_c_out));
  multiplicador multiplicador_1 (
    .A(registrador_3_q), .B(registrador_4_q), .C(registrador_6_q), .D(registrador_5_q), .in_5(in_13),
    .out_6(multiplicador_1_out_6), .out_7(multiplicador_1_out_7), .out_8(multiplicador_1_out_8),
    .out_9(multiplicador_1_out_9));
  and and_1 (and_1_out, registrador_5_q, registrador_6_q, registrador_7_q, registrador_8_q, registrador_4_q, registrador_3_q, registrador_2_q, registrador_1_q);
  Multiplexador multiplexador_1 (
    .in_1(somador_completo_1_s), .in_2(subtrator_completo_1_s), .in_3(multiplicador_1_out_9), .in_5(in_14),
    .in_6(in_15), .out_7(multiplexador_1_out_7));  // open: in_4
  Multiplexador multiplexador_2 (
    .in_1(somador_completo_3_s), .in_2(subtrator_completo_3_s), .in_3(multiplicador_1_out_7), .in_5(in_14),
    .in_6(in_15), .out_7(multiplexador_2_out_7));  // open: in_4
  Multiplexador multiplexador_3 (
    .in_1(somador_completo_4_s), .in_2(subtrator_completo_4_s), .in_3(multiplicador_1_out_6),
    .in_4(and_1_out), .in_5(in_14), .in_6(in_15), .out_7(multiplexador_3_out_7));
  Multiplexador multiplexador_4 (
    .in_1(somador_completo_2_s), .in_2(subtrator_completo_2_s), .in_3(multiplicador_1_out_8), .in_5(in_14),
    .in_6(in_15), .out_7(multiplexador_4_out_7));  // open: in_4
  registrador registrador_5 (.D(in_8), .enable(in_10), .Clock(in_16), .Q(registrador_5_q));  // open: Q_prime
  registrador registrador_6 (.D(in_7), .enable(in_10), .Clock(in_16), .Q(registrador_6_q));  // open: Q_prime
  registrador registrador_7 (.D(in_6), .enable(in_10), .Clock(in_16), .Q(registrador_7_q));  // open: Q_prime
  registrador registrador_8 (.D(in_5), .enable(in_10), .Clock(in_16), .Q(registrador_8_q));  // open: Q_prime
  registrador registrador_9 (.D(multiplexador_1_out_7), .enable(in_12), .Clock(in_16), .Q(out_18));  // open: Q_prime
  registrador registrador_10 (.D(multiplexador_4_out_7), .enable(in_12), .Clock(in_16), .Q(out_19));  // open: Q_prime
  registrador registrador_11 (.D(multiplexador_2_out_7), .enable(in_12), .Clock(in_16), .Q(out_20));  // open: Q_prime
  registrador registrador_12 (.D(multiplexador_3_out_7), .enable(in_12), .Clock(in_16), .Q(out_21));  // open: Q_prime
endmodule

module somador_completo (
  input  A,
  input  B,
  input  C,
  output S,
  output C_OUT
);

  wire and_1_out, and_2_out, and_3_out, xor_1_out;

  and and_1 (and_1_out, B, C);
  and and_2 (and_2_out, A, C);
  and and_3 (and_3_out, A, B);
  xor xor_1 (xor_1_out, A, B);
  or or_1 (C_OUT, and_1_out, and_2_out, and_3_out);
  xor xor_2 (S, xor_1_out, C);
endmodule

module subtrator_completo (
  input  A,
  input  B,
  input  C,
  output S,
  output C_OUT
);

  wire and_1_out, and_2_out, and_3_out, xor_1_out;

  and and_1 (and_1_out, B, C);
  and and_2 (and_2_out, ~A, C);  // AND_Gate
  and and_3 (and_3_out, ~A, B);  // AND_Gate
  xor xor_1 (xor_1_out, A, B);
  or or_1 (C_OUT, and_1_out, and_2_out, and_3_out);
  xor xor_2 (S, xor_1_out, C);
endmodule

module multiplicador (
  input  A,
  input  B,
  input  C,
  input  D,
  input  in_5,
  output out_6,
  output out_7,
  output out_8,
  output out_9
);

  wire and_1_out, and_2_out, and_3_out, and_4_out, and_5_out;

  and and_1 (and_1_out, A, D);
  and and_2 (and_2_out, B, D);
  and and_3 (and_3_out, A, C);
  and and_4 (and_4_out, B, C);
  xor xor_1 (out_8, and_1_out, and_4_out);
  and and_5 (and_5_out, and_1_out, and_4_out);
  xor xor_2 (out_9, and_2_out, in_5);
  xor xor_3 (out_7, and_3_out, and_5_out);
  and and_6 (out_6, and_3_out, and_5_out);

  // Notes on the sheet:
  //   DA
  //   DB
  //   CA
  //   CB
endmodule

module Multiplexador (
  input  in_1,
  input  in_2,
  input  in_3,
  input  in_4,
  input  in_5,
  input  in_6,
  output out_7
);

  wire and_1_out, and_2_out, and_3_out, and_4_out;

  and and_1 (and_1_out, in_1, ~in_5, ~in_6);  // AND_Gate
  and and_2 (and_2_out, in_2, ~in_5, in_6);  // AND_Gate
  and and_3 (and_3_out, in_3, in_5, ~in_6);  // AND_Gate
  and and_4 (and_4_out, in_4, in_5, in_6);
  or or_1 (out_7, and_1_out, and_2_out, and_3_out, and_4_out);
endmodule

module registrador (
  input  D,
  input  enable,
  input  Clock,
  output Q,
  output Q_prime
);

  wire and_1_out, nand_1_out, nand_2_out, not_1_out;

  not not_1 (not_1_out, D);
  and and_1 (and_1_out, enable, Clock);
  nand nand_1 (nand_1_out, D, and_1_out);
  nand nand_2 (nand_2_out, and_1_out, not_1_out);
  nand nand_3 (Q, nand_1_out, Q_prime);
  nand nand_4 (Q_prime, Q, nand_2_out);
endmodule

module main (
  input  [3:0] in_1,
  input  in_2,
  input  in_3,
  input  in_4,
  input  in_5,
  input  in_6,
  input  in_7,
  input  in_8,
  input  in_9,
  input  in_10,
  input  in_11
);

  wire clock_1_out;
  wire [3:0] ram_1_data, ula_1_out_18;

  Clock clock_1 (.out(clock_1_out));
  RAM #(.addrWidth(4), .dataWidth(4), .bus("separate")) ram_1 (
    .addr(in_1), .din(ula_1_out_18), .data(ram_1_data), .str(in_2), .clk(clock_1_out));  // open: sel, ld, clr
  ULA ula_1 (
    .in_9(in_3), .in_11(in_4), .in_13(in_5), .in_1(ram_1_data[3]), .in_2(ram_1_data[2]),
    .in_3(ram_1_data[1]), .in_4(ram_1_data[0]), .in_5(ram_1_data[3]), .in_6(ram_1_data[2]),
    .in_7(ram_1_data[1]), .in_8(ram_1_data[0]), .in_17(in_6), .in_14(in_7), .in_15(in_8), .in_16(in_9),
    .in_10(in_10), .in_12(in_11), .out_18(ula_1_out_18[0]), .out_19(ula_1_out_18[1]),
    .out_20(ula_1_out_18[2]), .out_21(ula_1_out_18[3]));
  Hex_Digit_Display hex_digit_display_1 (.value(ula_1_out_18));  // open: dp
endmodule
