// Logisim project Exercicio.circ as structural Verilog: 1 circuit, main circuit main
module main (
  input  B,
  input  in_2,
  input  C,
  input  D,
  output out_5
);

  wire and_1_out, and_2_out, and_3_out, nand_1_out, not_1_out, not_2_out, or_1_out;

  not not_1 (not_1_out, B);
  not not_2 (not_2_out, C);
  and and_1 (and_1_out, in_2, not_1_out);
  and and_2 (and_2_out, not_2_out, D);
  or or_1 (or_1_out, and_1_out, and_2_out);
  nand nand_1 (nand_1_out, in_2, D);
  and and_3 (and_3_out, not_1_out, C);
  or or_2 (out_5, nand_1_out, or_1_out, and_3_out);

  // Notes on the sheet:
  //   A
  //   S=[(A.-B)+(-C.D)]+-(A.D)+(-B.C)
endmodule
