// Logisim project TRABALHO 2 CIRCUITO SOMADOR HEX.circ as structural Verilog: 5 circuits, main circuit main
module main (
  input  B,
  input  A,
  input  B_2,
  input  A_2,
  input  B_3,
  input  A_3,
  input  A_4,
  input  B_4,
  input  C,
  input  D,
  input  C_2,
  input  in_12
);

  wire display_1_1_l1, display_1_1_l2, display_1_1_l3, display_1_1_l4, display_1_1_l5, display_1_1_l6,
       display_1_1_l7, display_2_1_l1, display_2_1_l2, display_2_1_l3, display_2_1_l4, display_2_1_l5,
       display_2_1_l6, display_2_1_l7, somador_completo_2_c_out, somador_completo_3_c_out;
  wire [3:0] multiplicador_1_out_9, somador_completo_3_s;

  Display_2 display_2_1 (
    .A(somador_completo_3_s[3]), .B(somador_completo_3_s[2]), .C(somador_completo_3_s[1]),
    .D(somador_completo_3_s[0]), .L1(display_2_1_l1), .L2(display_2_1_l2), .L3(display_2_1_l3),
    .L4(display_2_1_l4), .L5(display_2_1_l5), .L6(display_2_1_l6), .L7(display_2_1_l7));
  _7_Segment_Display u_7_segment_display_1 (
    .g(display_2_1_l7), .f(display_2_1_l6), .a(display_2_1_l1), .b(display_2_1_l2), .e(display_2_1_l5),
    .d(display_2_1_l4), .c(display_2_1_l3));  // open: dp
  somador_completo somador_completo_1 (
    .A(A), .B(B), .C(somador_completo_2_c_out), .S(somador_completo_3_s[2]), .C_OUT(somador_completo_3_s[3]));
  Display_1 display_1_1 (
    .A(somador_completo_3_s[3]), .B(somador_completo_3_s[2]), .C(somador_completo_3_s[1]),
    .D(somador_completo_3_s[0]), .L1(display_1_1_l1), .L2(display_1_1_l2), .L3(display_1_1_l3),
    .L4(display_1_1_l4), .L5(display_1_1_l5), .L6(display_1_1_l6), .L7(display_1_1_l7));
  _7_Segment_Display u_7_segment_display_2 (
    .g(display_1_1_l7), .f(display_1_1_l6), .a(display_1_1_l1), .b(display_1_1_l2), .e(display_1_1_l5),
    .d(display_1_1_l4), .c(display_1_1_l3));  // open: dp
  somador_completo somador_completo_2 (
    .A(A_2), .B(B_2), .C(somador_completo_3_c_out), .S(somador_completo_3_s[1]),
    .C_OUT(somador_completo_2_c_out));
  Hex_Digit_Display hex_digit_display_1 (.value(somador_completo_3_s));  // open: dp
  somador_completo somador_completo_3 (
    .A(A_3), .B(B_3), .C(C_2), .S(somador_completo_3_s[0]), .C_OUT(somador_completo_3_c_out));
  Hex_Digit_Display hex_digit_display_2 (.value(multiplicador_1_out_9));  // open: dp
  Multiplicador multiplicador_1 (
    .A(A_4), .B(B_4), .C(C), .D(D), .in_5(in_12), .out_6(multiplicador_1_out_9[3]),
    .out_7(multiplicador_1_out_9[2]), .out_8(multiplicador_1_out_9[1]), .out_9(multiplicador_1_out_9[0]));

  // Notes on the sheet:
  //   A
  //   B
  //   A
  //   HEX
  //   A
endmodule

module somador_completo (
  input  A,
  input  B,
  input  C,
  output S,
  output C_OUT
);

  wire and_1_out, and_2_out, and_3_out, xor_1_out;

  and and_1 (and_1_out, B, C);
  and and_2 (and_2_out, A, C);
  and and_3 (and_3_out, A, B);
  xor xor_1 (xor_1_out, A, B);
  or or_1 (C_OUT, and_1_out, and_2_out, and_3_out);
  xor xor_2 (S, xor_1_out, C);
endmodule

module Display_1 (
  input  A,
  input  B,
  input  C,
  input  D,
  output L1,
  output L2,
  output L3,
  output L4,
  output L5,
  output L6,
  output L7
);

  wire and_1_out, and_2_out, and_3_out, and_4_out, and_5_out, and_6_out, and_7_out, and_8_out, and_9_out,
       and_10_out, and_11_out, and_12_out, and_13_out, and_14_out, and_15_out, and_16_out, and_17_out,
       and_18_out, and_19_out, and_20_out, and_21_out, and_22_out, and_23_out, and_24_out, and_25_out,
       and_26_out, and_27_out, and_28_out, and_29_out, and_30_out, and_31_out, not_1_out, not_2_out,
       not_3_out, not_4_out, not_5_out, not_6_out, not_7_out, not_8_out, not_9_out, not_10_out, not_11_out,
       not_12_out, not_13_out, not_14_out, not_15_out, not_16_out, not_17_out, not_18_out, not_19_out,
       not_20_out, not_21_out, not_22_out, not_23_out, not_24_out, not_25_out, not_26_out, not_27_out,
       not_28_out, not_29_out, not_30_out, not_31_out, not_32_out, not_33_out, not_34_out, not_35_out,
       not_36_out, not_37_out, not_38_out, not_39_out, not_40_out, not_41_out, not_42_out, not_43_out;

  not not_1 (not_1_out, B);
  and and_1 (and_1_out, not_1_out, not_2_out);
  not not_2 (not_2_out, D);
  not not_3 (not_3_out, A);
  and and_2 (and_2_out, not_3_out, C);
  and and_3 (and_3_out, B, D);
  and and_4 (and_4_out, A, not_4_out);
  not not_4 (not_4_out, C);
  not not_5 (not_5_out, B);
  not not_6 (not_6_out, C);
  and and_5 (and_5_out, not_6_out, not_7_out);
  not not_7 (not_7_out, D);
  not not_8 (not_8_out, A);
  and and_6 (and_6_out, not_8_out, C, D);
  and and_7 (and_7_out, A, not_9_out);
  not not_9 (not_9_out, C);
  and and_8 (and_8_out, A, not_10_out);
  not not_10 (not_10_out, D);
  not not_11 (not_11_out, A);
  and and_9 (and_9_out, not_11_out, not_12_out);
  not not_12 (not_12_out, C);
  and and_10 (and_10_out, B, C);
  and and_11 (and_11_out, A, not_13_out);
  not not_13 (not_13_out, B);
  not not_14 (not_14_out, B);
  and and_12 (and_12_out, not_14_out, not_15_out);
  not not_15 (not_15_out, D);
  not not_16 (not_16_out, A);
  and and_13 (and_13_out, not_16_out, not_17_out, C);
  not not_17 (not_17_out, B);
  not not_18 (not_18_out, A);
  and and_14 (and_14_out, not_18_out, C, not_19_out);
  not not_19 (not_19_out, D);
  and and_15 (and_15_out, B, not_20_out, D);
  not not_20 (not_20_out, C);
  and and_16 (and_16_out, A, not_21_out);
  not not_21 (not_21_out, C);
  and and_17 (and_17_out, A, B, D);
  not not_22 (not_22_out, B);
  and and_18 (and_18_out, not_22_out, not_23_out);
  not not_23 (not_23_out, D);
  not not_24 (not_24_out, A);
  and and_19 (and_19_out, not_24_out, C, not_25_out);
  not not_25 (not_25_out, D);
  not not_26 (not_26_out, C);
  and and_20 (and_20_out, A, not_26_out, not_27_out);
  not not_27 (not_27_out, D);
  not not_28 (not_28_out, A);
  not not_29 (not_29_out, C);
  and and_21 (and_21_out, not_28_out, not_29_out, not_30_out);
  not not_30 (not_30_out, D);
  not not_31 (not_31_out, A);
  and and_22 (and_22_out, not_31_out, B, not_32_out);
  not not_32 (not_32_out, C);
  not not_33 (not_33_out, A);
  and and_23 (and_23_out, not_33_out, B, not_34_out);
  not not_34 (not_34_out, D);
  and and_24 (and_24_out, A, not_35_out, not_36_out);
  not not_35 (not_35_out, B);
  not not_36 (not_36_out, C);
  not not_37 (not_37_out, B);
  and and_25 (and_25_out, A, not_37_out, not_38_out);
  not not_38 (not_38_out, D);
  and and_26 (and_26_out, A, B, C);
  not not_39 (not_39_out, A);
  not not_40 (not_40_out, B);
  and and_27 (and_27_out, not_39_out, not_40_out, C);
  and and_28 (and_28_out, B, not_41_out);
  not not_41 (not_41_out, C);
  and and_29 (and_29_out, B, not_42_out);
  not not_42 (not_42_out, D);
  and and_30 (and_30_out, A, not_43_out);
  not not_43 (not_43_out, C);
  and and_31 (and_31_out, A, B);
  or or_1 (L1, and_1_out, and_2_out, and_3_out, and_4_out);
  or or_2 (L2, not_5_out, and_5_out, and_6_out, and_7_out, and_8_out);
  or or_3 (L3, and_9_out, D, and_10_out, and_11_out);
  or or_4 (L5, and_18_out, and_19_out, and_20_out);
  or or_5 (L7, and_27_out, and_28_out, and_29_out, and_30_out, and_31_out);
  or or_6 (L4, and_12_out, and_13_out, and_14_out, and_15_out, and_16_out, and_17_out);
  or or_7 (L6, and_21_out, and_22_out, and_23_out, and_24_out, and_25_out, and_26_out);
endmodule

module Display_2 (
  input  A,
  input  B,
  input  C,
  input  D,
  output L1,
  output L2,
  output L3,
  output L4,
  output L5,
  output L6,
  output L7
);

  wire and_1_out, and_2_out, and_3_out, and_4_out;

  and and_1 (and_1_out, A, C);
  and and_2 (and_2_out, A, B);
  and and_3 (and_3_out, A, C);
  and and_4 (and_4_out, A, B);
  or or_1 (L2, and_1_out, and_2_out);
  or or_2 (L3, and_3_out, and_4_out);

  assign L1 = 1'b0;
  assign L4 = 1'b0;
  assign L5 = 1'b0;
  assign L6 = 1'b0;
  assign L7 = 1'b0;
endmodule

module Multiplicador (
  input  A,
  input  B,
  input  C,
  input  D,
  input  in_5,
  output out_6,
  output out_7,
  output out_8,
  output out_9
);

  wire and_1_out, and_2_out, and_3_out, and_4_out, and_5_out;

  and and_1 (and_1_out, A, D);
  and and_2 (and_2_out, B, D);
  and and_3 (and_3_out, A, C);
  and and_4 (and_4_out, B, C);
  xor xor_1 (out_8, and_1_out, and_4_out);
  and and_5 (and_5_out, and_1_out, and_4_out);
  xor xor_2 (out_9, and_2_out, in_5);
  xor xor_3 (out_7, and_3_out, and_5_out);
  and and_6 (out_6, and_3_out, and_5_out);

  // Notes on the sheet:
  //   DA
  //   DB
  //   CA
  //   CB
endmodule
