// Logisim project memoria_ram.circ as structural Verilog: 1 circuit, main circuit main
module main (
  input  [7:0] \endereço ,
  input  [7:0] in_2,
  input  in_3,
  input  in_4,
  input  in_5,
  input  in_6,
  output [7:0] saida_de_dados
);

  wire clock_1_out;

  Clock clock_1 (.out(clock_1_out));
  RAM #(.bus("separate")) ram_1 (
    .addr(\endereço ), .din(in_2), .data(saida_de_dados), .str(in_5), .sel(in_3), .clk(clock_1_out),
    .ld(in_6), .clr(in_4));

  // Notes on the sheet:
  //   entrada de dados
  //   desabilita em nivel 0
  //   escreve na memoria em 1
  //   le da memória em 1
  //   dados
  //   limpa a memória em nivel 1
endmodule
