// Logisim project trabalho display final.circ as structural Verilog: 5 circuits, main circuit final
module \final  (
  input  in_1,
  input  in_2
);

  wire contador_1_out_2, contador_1_out_3, contador_1_out_4, controle_1_out_18, controle_1_out_19,
       controle_1_out_20, controle_1_out_21, controle_1_out_22, controle_1_out_23, controle_1_out_24,
       controle_1_out_25, n2000784_1_out_4, n2000784_1_out_5, n2000784_1_out_6, n2000784_1_out_7,
       n2000784_1_out_8, n2000784_1_out_9, n2000784_1_out_10, n2000784_1_out_11, n2000857_1_out_4,
       n2000857_1_out_5, n2000857_1_out_6, n2000857_1_out_7, n2000857_1_out_8, n2000857_1_out_9,
       n2000857_1_out_10, n2000857_1_out_11, undriven, undriven_2, undriven_3, undriven_4, undriven_5,
       undriven_6, undriven_7, undriven_8;

  contador contador_1 (.in_1(in_1), .out_2(contador_1_out_2), .out_3(contador_1_out_3), .out_4(contador_1_out_4));
  _2000857 u_2000857_1 (
    .A(contador_1_out_2), .B(contador_1_out_3), .C(contador_1_out_4), .out_4(n2000857_1_out_4),
    .out_5(n2000857_1_out_5), .out_6(n2000857_1_out_6), .out_7(n2000857_1_out_7), .out_8(n2000857_1_out_8),
    .out_9(n2000857_1_out_9), .out_10(n2000857_1_out_10), .out_11(n2000857_1_out_11));
  _7_Segment_Display u_7_segment_display_1 (
    .g(controle_1_out_18), .f(controle_1_out_19), .a(controle_1_out_20), .b(controle_1_out_21),
    .e(controle_1_out_22), .d(controle_1_out_23), .c(controle_1_out_24), .dp(controle_1_out_25));
  _2000784 u_2000784_1 (
    .A(contador_1_out_2), .B(contador_1_out_3), .C(contador_1_out_4), .out_4(n2000784_1_out_4),
    .out_5(n2000784_1_out_5), .out_6(n2000784_1_out_6), .out_7(n2000784_1_out_7), .out_8(n2000784_1_out_8),
    .out_9(n2000784_1_out_9), .out_10(n2000784_1_out_10), .out_11(n2000784_1_out_11));
  controle controle_1 (
    .in_2(n2000857_1_out_4), .in_4(n2000857_1_out_5), .in_6(n2000857_1_out_6), .in_8(n2000857_1_out_7),
    .in_10(n2000857_1_out_8), .in_12(n2000857_1_out_9), .in_14(n2000857_1_out_10), .in_16(n2000857_1_out_11),
    .in_1(in_2), .out_18(controle_1_out_18), .out_19(controle_1_out_19), .out_20(controle_1_out_20),
    .out_21(controle_1_out_21), .out_22(controle_1_out_22), .out_23(controle_1_out_23),
    .out_24(controle_1_out_24), .out_25(controle_1_out_25), .in_3(n2000784_1_out_4), .in_5(n2000784_1_out_5),
    .in_7(n2000784_1_out_6), .in_9(n2000784_1_out_7), .in_11(n2000784_1_out_8), .in_13(n2000784_1_out_9),
    .in_15(n2000784_1_out_10), .in_17(n2000784_1_out_11));
  _7_Segment_Display u_7_segment_display_2 (
    .g(undriven_5), .f(undriven_6), .a(undriven), .b(undriven_7), .e(undriven_4), .d(undriven_8),
    .c(undriven_3), .dp(undriven_2));
endmodule

module _2000857 (
  input  A,
  input  B,
  input  C,
  output out_4,
  output out_5,
  output out_6,
  output out_7,
  output out_8,
  output out_9,
  output out_10,
  output out_11
);

  wire A_nB_out, A_nC_out, B_nC_out, nA_B_out, nA_C_out, nA_nB_out, nA_nC_out, nB_C_out, nB_nC_out,
       not_1_out, not_2_out, not_3_out, not_4_out, not_5_out, not_6_out, not_7_out, not_8_out, not_9_out,
       not_10_out, not_11_out, not_12_out, not_13_out;

  not not_1 (not_1_out, B);
  not not_2 (not_2_out, B);
  not not_3 (not_3_out, A);
  not not_4 (not_4_out, A);
  not not_5 (not_5_out, B);
  not not_6 (not_6_out, A);
  not not_7 (not_7_out, C);
  not not_8 (not_8_out, C);
  not not_9 (not_9_out, B);
  not not_10 (not_10_out, C);
  not not_11 (not_11_out, C);
  not not_12 (not_12_out, A);
  not not_13 (not_13_out, B);
  and A_nB (A_nB_out, A, not_1_out);
  and nB_C (nB_C_out, not_2_out, C);
  and nA_C (nA_C_out, not_3_out, C);
  and nA_B (nA_B_out, not_4_out, B);
  and nA_nC (nA_nC_out, not_6_out, not_7_out);
  and A_nC (A_nC_out, A, not_8_out);
  and nB_nC (nB_nC_out, not_9_out, not_10_out);
  and B_nC (B_nC_out, B, not_11_out);
  and nA_nB (nA_nB_out, not_12_out, not_13_out);
  or u_a (out_4, A_nB_out, nB_nC_out);
  or u_b (out_5, A_nB_out, nB_C_out, nA_C_out, nA_B_out);
  or u_c (out_6, nA_C_out, not_5_out, nA_nC_out, A_nC_out);
  or d (out_7, nB_nC_out, B_nC_out, nA_nB_out, nA_C_out, nA_B_out);
  or e (out_8, nB_nC_out, nA_nC_out, nA_nB_out, nA_C_out, nA_B_out);
  or f (out_9, not_5_out, nA_C_out, nA_B_out, nA_nC_out);
  or g (out_10, A_nB_out, nB_C_out, nA_C_out, nA_B_out, A_nC_out);
  and h (out_11, A, B, C);
endmodule

module _2000784 (
  input  A,
  input  B,
  input  C,
  output out_4,
  output out_5,
  output out_6,
  output out_7,
  output out_8,
  output out_9,
  output out_10,
  output out_11
);

  wire A_nB_out, A_nC_out, and_1_out, and_2_out, and_3_out, B_nC_out, nA_B_out, nA_C_out, nA_nB_out,
       nA_nC_out, nB_C_out, not_1_out, not_2_out, not_3_out, not_4_out, not_5_out, not_6_out, not_7_out,
       not_8_out, not_9_out, not_10_out, not_11_out, not_12_out, not_13_out, not_14_out, not_15_out,
       not_16_out, or_1_out, or_2_out, or_3_out, or_4_out;

  not not_1 (not_1_out, A);
  not not_2 (not_2_out, C);
  not not_3 (not_3_out, B);
  not not_4 (not_4_out, B);
  not not_5 (not_5_out, C);
  not not_6 (not_6_out, A);
  not not_7 (not_7_out, A);
  not not_8 (not_8_out, B);
  not not_9 (not_9_out, C);
  not not_10 (not_10_out, B);
  not not_11 (not_11_out, A);
  not not_12 (not_12_out, C);
  not not_13 (not_13_out, C);
  not not_14 (not_14_out, A);
  not not_15 (not_15_out, B);
  not not_16 (not_16_out, B);
  and and_1 (and_1_out, not_1_out, not_2_out, not_3_out);
  and and_2 (and_2_out, A, not_4_out, C);
  and and_3 (and_3_out, A, B, not_5_out);
  and nA_B (nA_B_out, not_6_out, B);
  and nA_C (nA_C_out, not_7_out, C);
  and nB_C (nB_C_out, not_8_out, C);
  and B_nC (B_nC_out, B, not_9_out);
  and nA_nC (nA_nC_out, not_11_out, not_12_out);
  and A_nC (A_nC_out, A, not_13_out);
  and nA_nB (nA_nB_out, not_14_out, not_15_out);
  and A_nB (A_nB_out, A, not_16_out);
  or or_1 (or_1_out, not_10_out, nA_C_out, nA_B_out);
  or or_2 (or_2_out, nA_nC_out, B_nC_out, A_nC_out);
  or or_3 (or_3_out, nB_C_out, B_nC_out, A_nB_out);
  or or_4 (or_4_out, nA_C_out, nA_B_out, A_nC_out);
  or u_a (out_4, and_1_out, and_2_out, and_3_out);
  or u_b (out_5, nA_B_out, nA_C_out, B_nC_out, nB_C_out);
  or u_c (out_6, not_10_out, nA_C_out, nA_B_out, nA_nC_out);
  or d (out_7, or_1_out, or_2_out);
  or e (out_8, nA_nB_out, nB_C_out, nA_C_out, nA_nC_out, nA_B_out);
  or f (out_9, nB_C_out, nA_nB_out, nA_nC_out, nA_C_out, nA_B_out);
  or g (out_10, or_3_out, or_4_out);
  and h (out_11, A, B, C);
endmodule

module contador (
  input  in_1,
  output out_2,
  output out_3,
  output out_4
);

  wire clock_1_out, j_k_ff_1_qn, j_k_ff_2_qn;

  Clock clock_1 (.out(clock_1_out));
  J_K_Flip_Flop j_k_ff_1 (
    .J(in_1), .clk(clock_1_out), .K(in_1), .Q(out_4), .Qn(j_k_ff_1_qn), .en(in_1));  // open: preset, reset
  J_K_Flip_Flop j_k_ff_2 (
    .J(in_1), .clk(j_k_ff_1_qn), .K(in_1), .Q(out_3), .Qn(j_k_ff_2_qn), .en(in_1));  // open: preset, reset
  J_K_Flip_Flop j_k_ff_3 (.J(in_1), .clk(j_k_ff_2_qn), .K(in_1), .Q(out_2), .en(in_1));  // open: Qn, preset, reset
endmodule

module controle (
  input  in_1,
  input  in_2,
  input  in_3,
  input  in_4,
  input  in_5,
  input  in_6,
  input  in_7,
  input  in_8,
  input  in_9,
  input  in_10,
  input  in_11,
  input  in_12,
  input  in_13,
  input  in_14,
  input  in_15,
  input  in_16,
  input  in_17,
  output out_18,
  output out_19,
  output out_20,
  output out_21,
  output out_22,
  output out_23,
  output out_24,
  output out_25
);

  wire and_1_out, and_2_out, and_3_out, and_4_out, and_5_out, and_6_out, and_7_out, and_8_out, and_9_out,
       and_10_out, and_11_out, and_12_out, and_13_out, and_14_out, and_15_out, and_16_out, not_1_out;

  and and_1 (and_1_out, in_2, in_1);
  and and_2 (and_2_out, in_4, in_1);
  and and_3 (and_3_out, in_6, in_1);
  and and_4 (and_4_out, in_8, in_1);
  and and_5 (and_5_out, in_10, in_1);
  and and_6 (and_6_out, in_12, in_1);
  and and_7 (and_7_out, in_14, in_1);
  and and_8 (and_8_out, in_16, in_1);
  or or_1 (out_18, and_1_out, and_9_out);
  or or_2 (out_19, and_2_out, and_10_out);
  or or_3 (out_20, and_3_out, and_11_out);
  or or_4 (out_21, and_4_out, and_12_out);
  or or_5 (out_22, and_5_out, and_13_out);
  or or_6 (out_23, and_6_out, and_14_out);
  or or_7 (out_24, and_7_out, and_15_out);
  or or_8 (out_25, and_8_out, and_16_out);
  and and_9 (and_9_out, in_3, not_1_out);
  and and_10 (and_10_out, in_5, not_1_out);
  and and_11 (and_11_out, in_7, not_1_out);
  and and_12 (and_12_out, in_9, not_1_out);
  and and_13 (and_13_out, in_11, not_1_out);
  and and_14 (and_14_out, in_13, not_1_out);
  and and_15 (and_15_out, in_15, not_1_out);
  not not_1 (not_1_out, in_1);
  and and_16 (and_16_out, in_17, not_1_out);
endmodule
