// Logisim project trabalho display(minha parte).circ as structural Verilog: 2 circuits, main circuit main
module main (
  input  A,
  input  B,
  input  C,
  output L1,
  output L2,
  output L3,
  output L4,
  output L5,
  output L6,
  output L7
);

  wire and_1_out, and_2_out, and_3_out, and_4_out, and_5_out, and_6_out, and_7_out, and_8_out, and_9_out,
       and_10_out, and_11_out, and_12_out, not_1_out, not_2_out, not_3_out, not_4_out, not_5_out, not_6_out,
       not_7_out, not_8_out, not_9_out, not_10_out, not_11_out, not_12_out, not_13_out, not_14_out,
       not_15_out, not_16_out, not_17_out, not_18_out, not_19_out, not_20_out, not_21_out;

  not not_1 (not_1_out, A);
  not not_2 (not_2_out, B);
  not not_3 (not_3_out, A);
  not not_4 (not_4_out, B);
  not not_5 (not_5_out, C);
  not not_6 (not_6_out, A);
  not not_7 (not_7_out, A);
  not not_8 (not_8_out, B);
  not not_9 (not_9_out, C);
  not not_10 (not_10_out, B);
  not not_11 (not_11_out, B);
  not not_12 (not_12_out, B);
  not not_13 (not_13_out, A);
  not not_14 (not_14_out, C);
  not not_15 (not_15_out, A);
  not not_16 (not_16_out, B);
  not not_17 (not_17_out, C);
  not not_18 (not_18_out, B);
  not not_19 (not_19_out, C);
  or or_1 (L1, not_1_out, not_2_out);
  or or_2 (L2, not_3_out, not_4_out, not_5_out);
  and and_1 (and_1_out, not_6_out, C);
  and and_2 (and_2_out, not_7_out, B);
  and and_3 (and_3_out, A, not_8_out);
  and and_4 (and_4_out, A, not_9_out);
  not not_20 (not_20_out, A);
  and and_5 (and_5_out, not_10_out, C);
  not not_21 (not_21_out, A);
  and and_6 (and_6_out, not_11_out, C);
  and and_7 (and_7_out, not_12_out, C);
  and and_8 (and_8_out, not_13_out, B);
  and and_9 (and_9_out, B, not_14_out);
  and and_10 (and_10_out, not_15_out, not_16_out, not_17_out);
  and and_11 (and_11_out, A, not_18_out, C);
  and and_12 (and_12_out, A, B, not_19_out);
  or or_3 (L3, and_1_out, and_2_out, and_3_out, and_4_out);
  or or_4 (L4, not_20_out, and_5_out);
  or or_5 (L5, not_21_out, and_6_out);
  or or_6 (L6, and_7_out, and_8_out, and_9_out);
  or or_7 (L7, and_10_out, and_11_out, and_12_out);
endmodule

module CAIO (
);

  wire clock_1_out, main_1_l1, main_1_l2, main_1_l3, main_1_l4, main_1_l5, main_1_l6, main_1_l7;
  wire [2:0] counter_1_q;

  Counter #(.width(3), .max('h7)) counter_1 (.Q(counter_1_q), .clk(clock_1_out));  // open: load, D, count, carry, clr
  Clock clock_1 (.out(clock_1_out));
  main main_1 (
    .A(counter_1_q[2]), .B(counter_1_q[1]), .C(counter_1_q[0]), .L1(main_1_l1), .L2(main_1_l2),
    .L3(main_1_l3), .L4(main_1_l4), .L5(main_1_l5), .L6(main_1_l6), .L7(main_1_l7));
  _7_Segment_Display u_7_segment_display_1 (
    .g(main_1_l7), .f(main_1_l6), .a(main_1_l1), .b(main_1_l2), .e(main_1_l5), .d(main_1_l4), .c(main_1_l3));  // open: dp
endmodule
